// Logisim project ALU.circ as structural Verilog: 5 circuits, main circuit main
module main (
  input  Cin,
  input  DAA,
  input  DSA,
  input  in_4,
  input  [7:0] B,
  input  in_6,
  input  [7:0] A,
  input  [4:0] Select_And_Eor_Sum_Sr_Or,
  output V,
  output HC,
  output Cout
);

  wire [3:0] dec_adjust_adder_1_out, dec_adjust_adder_2_out;
  wire [7:0] alu_8bit_1_out, controlled_buffer_1_out;

  assign controlled_buffer_1_out = in_4 ? B : 8'bz;  // Controlled_Buffer controlled_buffer_1
  assign controlled_buffer_1_out = in_6 ? ~B : 8'bz;  // Controlled_Inverter controlled_inverter_1
  ALU_8bit alu_8bit_1 (
    .B(controlled_buffer_1_out), .A(A), .Cin(Cin), .DAA(DAA), .V(V), .HC(HC), .Cout(Cout),
    .Out(alu_8bit_1_out), .Select_And_Eor_Sum_Sr_Or(Select_And_Eor_Sum_Sr_Or));
  Dec_adjust_adder dec_adjust_adder_1 (
    .In(alu_8bit_1_out[3:0]), .DSA(DSA), .DAA(DAA), .Cin(HC), .Out(dec_adjust_adder_1_out));
  Dec_adjust_adder dec_adjust_adder_2 (
    .In(alu_8bit_1_out[7:4]), .DSA(DSA), .DAA(DAA), .Cin(Cout), .Out(dec_adjust_adder_2_out));
  Hex_Digit_Display hex_digit_display_1 (.value(dec_adjust_adder_2_out));  // open: dp
  Hex_Digit_Display hex_digit_display_2 (.value(dec_adjust_adder_1_out));  // open: dp
endmodule

module ALU_1bit (
  input  Cin,
  input  SRin,
  input  B,
  input  A,
  input  [4:0] Select_And_Eor_Sum_Sr_Or,
  output Out,
  output Cout,
  output SRout
);

  wire and_2_out, or_1_out, xor_1_out, xor_2_out;

  or or_1 (or_1_out, A, B);
  and and_1 (SRout, A, B);
  or or_2 (Cout, SRout, and_2_out);
  xor xor_1 (xor_1_out, B, A);
  and and_2 (and_2_out, Cin, xor_1_out);
  xor xor_2 (xor_2_out, Cin, xor_1_out);
  assign Out = Select_And_Eor_Sum_Sr_Or[4] ? SRout : 1'bz;  // Controlled_Buffer ANDS
  assign Out = Select_And_Eor_Sum_Sr_Or[1] ? SRin : 1'bz;  // Controlled_Buffer SRS
  assign Out = Select_And_Eor_Sum_Sr_Or[2] ? xor_2_out : 1'bz;  // Controlled_Buffer SUMS
  assign Out = Select_And_Eor_Sum_Sr_Or[3] ? xor_1_out : 1'bz;  // Controlled_Buffer EORS
  assign Out = Select_And_Eor_Sum_Sr_Or[0] ? or_1_out : 1'bz;  // Controlled_Buffer ORS
endmodule

module ALU_4bit (
  input  Cin,
  input  [3:0] B,
  input  [4:0] Select_And_Eor_Sum_Sr_Or,
  input  DAA,
  input  [3:0] A,
  input  SRin,
  output SRout,
  output [3:0] Out,
  output Cn_1,
  output COut
);

  wire alu_1bit_1_cout, alu_1bit_2_cout, alu_1bit_2_srout, alu_1bit_3_srout, alu_1bit_4_cout,
       alu_1bit_4_srout, and_1_out, and_2_out;

  ALU_1bit alu_1bit_1 (
    .B(B[0]), .A(A[0]), .Cin(Cin), .SRout(SRout), .Cout(alu_1bit_1_cout), .SRin(alu_1bit_2_srout),
    .Out(Out[0]), .Select_And_Eor_Sum_Sr_Or(Select_And_Eor_Sum_Sr_Or));
  ALU_1bit alu_1bit_2 (
    .B(B[1]), .A(A[1]), .Cin(alu_1bit_1_cout), .SRout(alu_1bit_2_srout), .Cout(alu_1bit_2_cout),
    .SRin(alu_1bit_3_srout), .Out(Out[1]), .Select_And_Eor_Sum_Sr_Or(Select_And_Eor_Sum_Sr_Or));
  ALU_1bit alu_1bit_3 (
    .B(B[2]), .A(A[2]), .Cin(alu_1bit_2_cout), .SRout(alu_1bit_3_srout), .Cout(Cn_1),
    .SRin(alu_1bit_4_srout), .Out(Out[2]), .Select_And_Eor_Sum_Sr_Or(Select_And_Eor_Sum_Sr_Or));
  ALU_1bit alu_1bit_4 (
    .B(B[3]), .A(A[3]), .Cin(Cn_1), .SRout(alu_1bit_4_srout), .Cout(alu_1bit_4_cout), .SRin(SRin),
    .Out(Out[3]), .Select_And_Eor_Sum_Sr_Or(Select_And_Eor_Sum_Sr_Or));
  or or_1 (COut, alu_1bit_4_cout, and_1_out, and_2_out);
  and and_1 (and_1_out, Out[3], Out[2], DAA);
  and and_2 (and_2_out, Out[3], Out[1], DAA);
endmodule

module ALU_8bit (
  input  Cin,
  input  DAA,
  input  [7:0] B,
  input  [4:0] Select_And_Eor_Sum_Sr_Or,
  input  [7:0] A,
  output [7:0] Out,
  output HC,
  output V,
  output Cout
);

  wire alu_4bit_1_srout, alu_4bit_2_cn_1, alu_4bit_2_cout, alu_4bit_2_srout;

  xor xor_1 (V, alu_4bit_2_cn_1, alu_4bit_2_cout);
  ALU_4bit alu_4bit_1 (
    .B(B[3:0]), .A(A[3:0]), .Cin(Cin), .SRout(alu_4bit_1_srout), .DAA(DAA), .COut(HC),
    .SRin(alu_4bit_2_srout), .Out(Out[3:0]), .Select_And_Eor_Sum_Sr_Or(Select_And_Eor_Sum_Sr_Or));  // open: Cn_1
  ALU_4bit alu_4bit_2 (
    .B(B[7:4]), .A(A[7:4]), .Cin(HC), .SRout(alu_4bit_2_srout), .DAA(DAA), .COut(alu_4bit_2_cout),
    .SRin(Cin), .Cn_1(alu_4bit_2_cn_1), .Out(Out[7:4]), .Select_And_Eor_Sum_Sr_Or(Select_And_Eor_Sum_Sr_Or));
  Multiplexer #(.enable("false")) multiplexer_1 (
    .in0(alu_4bit_2_cout), .in1(alu_4bit_1_srout), .out(Cout), .sel(Select_And_Eor_Sum_Sr_Or[1]));
endmodule

module Dec_adjust_adder (
  input  [3:0] In,
  input  DSA,
  input  DAA,
  input  Cin,
  output [3:0] Out
);

  wire not_1_out;
  wire [3:1] or_1_out;

  not not_1 (not_1_out, Cin);
  and and_1 (or_1_out[2], DAA, Cin);
  and and_2 (or_1_out[3], DSA, not_1_out);
  or or_1 (or_1_out[1], or_1_out[2], or_1_out[3]);
  Adder #(.width(4)) adder_1 (.a(In), .b({or_1_out, 1'b0}), .out(Out));  // open: cin, cout
endmodule
