// Logisim project chargen.circ as structural Verilog: 1 circuit, main circuit main
module main (
);

  wire button_1_out, clock_1_out, not_1_out;
  wire [2:0] counter_1_q;
  wire [7:0] demultiplexer_1_out0, demultiplexer_1_out1, demultiplexer_1_out2, demultiplexer_1_out3,
       demultiplexer_1_out4, demultiplexer_1_out5, demultiplexer_1_out6, demultiplexer_1_out7, rom_1_data;
  wire [8:0] counter_2_q;

  Clock clock_1 (.out(clock_1_out));
  Button button_1 (.out(button_1_out));
  Counter #(.width(3), .max('h7)) counter_1 (.Q(counter_1_q), .clk(clock_1_out));  // open: load, D, count, carry, clr
  Counter #(.width(9), .max('h1ff)) counter_2 (
    .Q(counter_2_q), .clk(button_1_out));  // open: load, D, count, carry, clr
  not not_1 (not_1_out, clock_1_out);
  ROM #(.addrWidth(12)) rom_1 (.addr({counter_2_q, counter_1_q}), .data(rom_1_data));  // open: sel
  Demultiplexer #(.select(3), .width(8), .disabled(0)) demultiplexer_1 (
    .out0(demultiplexer_1_out0), .out1(demultiplexer_1_out1), .out2(demultiplexer_1_out2),
    .out3(demultiplexer_1_out3), .out4(demultiplexer_1_out4), .out5(demultiplexer_1_out5),
    .out6(demultiplexer_1_out6), .out7(demultiplexer_1_out7), .in(rom_1_data), .sel(counter_1_q),
    .en(not_1_out));
  DotMatrix #(.inputtype("row"), .matrixcols(8), .matrixrows(8), .persist(16)) dotmatrix_1 (
    .row0(demultiplexer_1_out0), .row1(demultiplexer_1_out1), .row2(demultiplexer_1_out2),
    .row3(demultiplexer_1_out3), .row4(demultiplexer_1_out4), .row5(demultiplexer_1_out5),
    .row6(demultiplexer_1_out6), .row7(demultiplexer_1_out7));

  // Notes on the sheet:
  //   by ir. Marc Dendooven
  //   Commodore 64 Character ROM to LED
  //   contents of rom_1 (hex, n*v repeats v):
  //   3c 66 6e 6e 60 62 3c 0 18 3c 66 7e 66 66 66 0 7c 66 66 7c 66 66 7c 0 3c 66 60 60 60 66 3c 0 78 6c 66
  //   66 66 6c 78 0 7e 60 60 78 60 60 7e 0 7e 60 60 78 60 60 60 0 3c 66 60 6e 66 66 3c 0 66 66 66 7e 66 66
  //   66 0 3c 5*18 3c 0 1e 4*c 6c 38 0 66 6c 78 70 78 6c 66 0 6*60 7e 0 63 77 7f 6b 63 63 63 0 66 76 7e 7e
  //   6e 66 66 0 3c 5*66 3c 0 7c 66 66 7c 60 60 60 0 3c 4*66 3c e 0 7c 66 66 7c 78 6c 66 0 3c 66 60 3c 6
  //   66 3c 0 7e 6*18 0 6*66 3c 0 5*66 3c 18 0 63 63 63 6b 7f 77 63 0 66 66 3c 18 3c 66 66 0 66 66 66 3c
  //   18 18 18 0 7e 6 c 18 30 60 7e 0 3c 5*30 3c 0 c 12 30 7c 30 62 fc 0 3c 5*c 3c 0 0 18 3c 7e 4*18 0 10
  //   30 7f 7f 30 10 9*0 4*18 0 0 18 0 66 66 66 5*0 66 66 ff 66 ff 66 66 0 18 3e 60 3c 6 7c 18 0 62 66 c
  //   18 30 66 46 0 3c 66 3c 38 67 66 3f 0 6 c 18 5*0 c 18 30 30 30 18 c 0 30 18 c c c 18 30 0 0 66 3c ff
  //   3c 66 0 0 0 18 18 7e 18 18 7*0 18 18 30 0 0 0 7e 9*0 18 18 0 0 3 6 c 18 30 60 0 3c 66 6e 76 66 66 3c
  //   0 18 18 38 18 18 18 7e 0 3c 66 6 c 30 60 7e 0 3c 66 6 1c 6 66 3c 0 6 e 1e 66 7f 6 6 0 7e 60 7c 6 6
  //   66 3c 0 3c 66 60 7c 66 66 3c 0 7e 66 c 4*18 0 3c 66 66 3c 66 66 3c 0 3c 66 66 3e 6 66 3c 0 0 0 18 0
  //   0 18 4*0 18 0 0 18 18 30 e 18 30 60 30 18 e 0 0 0 7e 0 7e 0 0 0 70 18 c 6 c 18 70 0 3c 66 6 c 18 0
  //   18 4*0 ff ff 0 0 0 8 1c 3e 7f 7f 1c 3e 0 8*18 0 0 0 ff ff 5*0 ff ff 5*0 ff ff 9*0 ff ff 0 0 8*30 8*c
  //   0 0 0 e0 f0 38 4*18 1c f 7 0 0 0 18 18 38 f0 e0 0 0 0 6*c0 ff ff c0 e0 70 38 1c e 7 3 3 7 e 1c 38 70
  //   e0 c0 ff ff 6*c0 ff ff 6*3 0 3c 4*7e 3c 6*0 ff ff 0 36 7f 7f 7f 3e 1c 8 0 8*60 0 0 0 7 f 1c 18 18 c3
  //   e7 7e 3c 3c 7e e7 c3 0 3c 7e 66 66 7e 3c 0 18 18 66 66 18 18 3c 0 8*6 8 1c 3e 7f 3e 1c 8 0 18 18 18
  //   ff ff 18 18 18 c0 c0 30 30 c0 c0 30 30 8*18 0 0 3 3e 76 36 36 0 ff 7f 3f 1f f 7 3 1 8*0 8*f0 4*0
  //   5*ff 14*0 ff 8*c0 cc cc 33 33 cc cc 33 33 8*3 4*0 cc cc 33 33 ff fe fc f8 f0 e0 c0 80 8*3 18 18 18
  //   1f 1f 18 18 18 4*0 4*f 18 18 18 1f 1f 6*0 f8 f8 18 18 18 6*0 ff ff 0 0 0 1f 1f 6*18 ff ff 6*0 ff ff
  //   6*18 f8 f8 18 18 18 8*c0 8*e0 8*7 ff ff 6*0 ff ff ff 10*0 ff ff ff 6*3 ff ff 4*0 4*f0 4*f 4*0 18 18
  //   18 f8 f8 0 0 0 4*f0 4*0 4*f0 4*f c3 99 91 91 9f 99 c3 ff e7 c3 99 81 99 99 99 ff 83 99 99 83 99 99
  //   83 ff c3 99 9f 9f 9f 99 c3 ff 87 93 99 99 99 93 87 ff 81 9f 9f 87 9f 9f 81 ff 81 9f 9f 87 9f 9f 9f
  //   ff c3 99 9f 91 99 99 c3 ff 99 99 99 81 99 99 99 ff c3 5*e7 c3 ff e1 4*f3 93 c7 ff 99 93 87 8f 87 93
  //   99 ff 6*9f 81 ff 9c 88 80 94 9c 9c 9c ff 99 89 81 81 91 99 99 ff c3 5*99 c3 ff 83 99 99 83 9f 9f 9f
  //   ff c3 4*99 c3 f1 ff 83 99 99 83 87 93 99 ff c3 99 9f c3 f9 99 c3 ff 81 6*e7 ff 6*99 c3 ff 5*99 c3 e7
  //   ff 9c 9c 9c 94 80 88 9c ff 99 99 c3 e7 c3 99 99 ff 99 99 99 c3 e7 e7 e7 ff 81 f9 f3 e7 cf 9f 81 ff
  //   c3 5*cf c3 ff f3 ed cf 83 cf 9d 3 ff c3 5*f3 c3 ff ff e7 c3 81 4*e7 ff ef cf 80 80 cf ef 9*ff 4*e7
  //   ff ff e7 ff 99 99 99 5*ff 99 99 0 99 0 99 99 ff e7 c1 9f c3 f9 83 e7 ff 9d 99 f3 e7 cf 99 b9 ff c3
  //   99 c3 c7 98 99 c0 ff f9 f3 e7 5*ff f3 e7 cf cf cf e7 f3 ff cf e7 f3 f3 f3 e7 cf ff ff 99 c3 0 c3 99
  //   ff ff ff e7 e7 81 e7 e7 7*ff e7 e7 cf ff ff ff 81 9*ff e7 e7 ff ff fc f9 f3 e7 cf 9f ff c3 99 91 89
  //   99 99 c3 ff e7 e7 c7 e7 e7 e7 81 ff c3 99 f9 f3 cf 9f 81 ff c3 99 f9 e3 f9 99 c3 ff f9 f1 e1 99 80
  //   f9 f9 ff 81 9f 83 f9 f9 99 c3 ff c3 99 9f 83 99 99 c3 ff 81 99 f3 4*e7 ff c3 99 99 c3 99 99 c3 ff c3
  //   99 99 c1 f9 99 c3 ff ff ff e7 ff ff e7 4*ff e7 ff ff e7 e7 cf f1 e7 cf 9f cf e7 f1 ff ff ff 81 ff 81
  //   ff ff ff 8f e7 f3 f9 f3 e7 8f ff c3 99 f9 f3 e7 ff e7 4*ff 0 0 ff ff ff f7 e3 c1 80 80 e3 c1 ff 8*e7
  //   ff ff ff 0 0 5*ff 0 0 5*ff 0 0 9*ff 0 0 ff ff 8*cf 8*f3 ff ff ff 1f f c7 4*e7 e3 f0 f8 ff ff ff e7
  //   e7 c7 f 1f ff ff ff 6*3f 0 0 3f 1f 8f c7 e3 f1 f8 fc fc f8 f1 e3 c7 8f 1f 3f 0 0 6*3f 0 0 6*fc ff c3
  //   4*81 c3 6*ff 0 0 ff c9 80 80 80 c1 e3 f7 ff 8*9f ff ff ff f8 f0 e3 e7 e7 3c 18 81 c3 c3 81 18 3c ff
  //   c3 81 99 99 81 c3 ff e7 e7 99 99 e7 e7 c3 ff 8*f9 f7 e3 c1 80 c1 e3 f7 ff e7 e7 e7 0 0 e7 e7 e7 3f
  //   3f cf cf 3f 3f cf cf 8*e7 ff ff fc c1 89 c9 c9 ff 0 80 c0 e0 f0 f8 fc fe 8*ff 8*f 4*ff 5*0 14*ff 0
  //   8*3f 33 33 cc cc 33 33 cc cc 8*fc 4*ff 33 33 cc cc 0 1 3 7 f 1f 3f 7f 8*fc e7 e7 e7 e0 e0 e7 e7 e7
  //   4*ff 4*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
endmodule
