// Logisim project harvard.circ as structural Verilog: 4 circuits, main circuit Datapad
module main (
  output [9:0] out_1
);

  wire and_1_out, and_2_out, and_3_out, datapad_1_n, datapad_1_z;
  wire [7:0] and_4_out;
  wire [7:7] or_1_out;

  and and_1 (and_1_out, datapad_1_n, out_1[9]);
  or or_1 (or_1_out[7], and_1_out, and_2_out, and_3_out);
  and and_2 (and_2_out, out_1[9], out_1[8]);
  and and_3 (and_3_out, datapad_1_z, out_1[8]);
  assign and_4_out = {8{or_1_out[7]}} & out_1[7:0];  // AND_Gate and_4, 8 bits wide
  Datapad datapad_1 (
    .W_DP(and_4_out[4]), .W_DM(and_4_out[5]), .W_PC(and_4_out[6]), .W_A(and_4_out[7]), .N(datapad_1_n),
    .Z(datapad_1_z), .Control(out_1), .R_DM(and_4_out[3]), .R_H(and_4_out[2]), .R_A(and_4_out[1]),
    .Sub(and_4_out[0]));

  // Notes on the sheet:
  //   ED1 - (c)2018 by ir. Marc Dendooven
endmodule

module Datapad (
  input  W_DP,
  input  R_DM,
  input  W_DM,
  input  W_PC,
  input  R_H,
  input  W_A,
  input  R_A,
  input  Sub,
  output [9:0] Control,
  output N,
  output Z
);

  wire Clk, nor_1_out, not_1_out, not_2_out;
  wire [7:0] A_q, ALU_out, controlled_buffer_1_out, controlled_buffer_3_out, DP_q, H_q, PC_q, ram_1_data;

  Clock clock_1 (.out(Clk));
  not not_1 (not_1_out, W_PC);
  Register #(.trigger("falling")) DP (.D(ALU_out), .en(W_DP), .Q(DP_q), .clk(Clk));  // open: clr
  Counter #(.trigger("falling")) PC (
    .load(W_PC), .D(ALU_out), .count(not_1_out), .Q(PC_q), .clk(Clk));  // open: carry, clr
  Register #(.trigger("falling")) A (.D(ALU_out), .en(W_A), .Q(A_q), .clk(Clk));  // open: clr
  Test test_1 (.IN(A_q), .N(N), .Z(Z));
  not not_2 (not_2_out, Clk);
  RAM #(.bus("separate")) ram_1 (
    .addr(DP_q), .din(ALU_out), .data(ram_1_data), .str(W_DM), .clk(not_2_out));  // open: sel, ld, clr
  ROM #(.dataWidth(10)) rom_1 (.addr(PC_q), .data(Control));  // open: sel
  nor nor_1 (nor_1_out, Control[8], Control[9]);
  Register #(.trigger("falling")) H (.D(Control[7:0]), .en(nor_1_out), .Q(H_q), .clk(Clk));  // open: clr
  assign controlled_buffer_1_out = R_DM ? ram_1_data : 8'bz;  // Controlled_Buffer controlled_buffer_1
  assign controlled_buffer_1_out = R_H ? H_q : 8'bz;  // Controlled_Buffer controlled_buffer_2
  assign controlled_buffer_3_out = R_A ? A_q : 8'bz;  // Controlled_Buffer controlled_buffer_3
  ALU ALU (.Sub(Sub), .A(controlled_buffer_3_out), .B(controlled_buffer_1_out), .Out(ALU_out));

  // Notes on the sheet:
  //   Data Memory
  //   Program memory
  //   contents of rom_1 (hex, n*v repeats v):
  //   2 314 320 310 388 18 144 2 314 388 1 314 38a 2 314 322 310 388 1 387 322 4 344 18 344
  //   ED1 - (c)2018 by ir. Marc Dendooven
endmodule

module Test (
  input  [7:0] IN,
  output N,
  output Z
);

  nor nor_1 (Z, IN[7], IN[6], IN[5], IN[4], IN[3], IN[2], IN[1], IN[0]);

  assign N = IN[7];

  // Notes on the sheet:
  //   ED1 - (c)2018 by ir. Marc Dendooven
endmodule

module ALU (
  input  Sub,
  input  [7:0] A,
  input  [7:0] B,
  output [7:0] Out
);

  wire [7:0] xor_1_out;

  assign xor_1_out = B ^ {8{Sub}};  // XOR_Gate xor_1, 8 bits wide
  Adder adder_1 (.a(xor_1_out), .b(A), .out(Out), .cin(Sub));  // open: cout

  // Notes on the sheet:
  //   A: pull=down
  //   B: pull=down
  //   ED1 - (c)2018 by ir. Marc Dendooven
endmodule
