// Logisim project mic1.circ as structural Verilog: 7 circuits, main circuit main
module main (
);


  // Notes on the sheet:
  //   Andrew Tanenbaum's MIC1
  //   adapted for Logisim by ir. Marc Dendooven
endmodule

module _1bit_ALU (
  input  Cin,
  input  A,
  input  B,
  input  [4:0] control,
  output \output ,
  output Cout
);

  wire A_B_out, AB_out, and_1_out, and_2_out, and_3_out, and_4_out, and_5_out, and_6_out, and_7_out,
       and_8_out, and_9_out, and_10_out, and_11_out, and_12_out, nB_out, not_1_out, not_2_out, not_3_out,
       not_4_out, xor_1_out, xor_2_out, xor_3_out;

  Pull_Resistor pull_resistor_1 (.node(A));
  Pull_Resistor pull_resistor_2 (.node(B));
  and and_1 (and_1_out, A, control[2]);
  and and_2 (and_2_out, B, control[1]);
  not not_1 (not_1_out, control[4]);
  not not_2 (not_2_out, control[3]);
  not not_3 (not_3_out, control[4]);
  not not_4 (not_4_out, control[3]);
  xor xor_1 (xor_1_out, control[0], and_1_out);
  and and_3 (and_3_out, not_1_out, not_2_out);
  and and_4 (and_4_out, not_3_out, control[3]);
  and and_5 (and_5_out, control[4], not_4_out);
  and and_6 (and_6_out, control[4], control[3]);
  and AB (AB_out, xor_1_out, and_2_out);
  or A_B (A_B_out, xor_1_out, and_2_out);
  not nB (nB_out, and_2_out);
  and and_7 (and_7_out, AB_out, and_3_out);
  and and_8 (and_8_out, A_B_out, and_4_out);
  and and_9 (and_9_out, nB_out, and_5_out);
  and and_10 (and_10_out, and_6_out, xor_1_out, and_2_out);
  xor xor_2 (xor_2_out, and_2_out, xor_1_out);
  and and_11 (and_11_out, and_6_out, xor_2_out, Cin);
  or or_1 (Cout, and_10_out, and_11_out);
  xor xor_3 (xor_3_out, Cin, xor_2_out);
  and and_12 (and_12_out, xor_3_out, and_6_out);
  or or_2 (\output , and_7_out, and_8_out, and_9_out, and_12_out);

  // Notes on the sheet:
  //   control bits: 0=INVA, 1=ENB, 2=ENA, 3=F1, 4=F0
  //   sum
endmodule

module _8bit_ALU (
  input  Cin,
  input  [7:0] A,
  input  [7:0] B,
  input  [4:0] Control,
  output [7:0] Output,
  output Cout
);

  wire n1bit_alu_1_cout, n1bit_alu_2_cout, n1bit_alu_3_cout, n1bit_alu_4_cout, n1bit_alu_5_cout,
       n1bit_alu_6_cout, n1bit_alu_7_cout;

  _1bit_ALU u_1bit_alu_1 (
    .A(A[0]), .B(B[0]), .control(Control), .Cin(Cin), .Cout(n1bit_alu_1_cout), .\output (Output[0]));
  _1bit_ALU u_1bit_alu_2 (
    .A(A[1]), .B(B[1]), .control(Control), .Cin(n1bit_alu_1_cout), .Cout(n1bit_alu_2_cout),
    .\output (Output[1]));
  _1bit_ALU u_1bit_alu_3 (
    .A(A[2]), .B(B[2]), .control(Control), .Cin(n1bit_alu_2_cout), .Cout(n1bit_alu_3_cout),
    .\output (Output[2]));
  _1bit_ALU u_1bit_alu_4 (
    .A(A[3]), .B(B[3]), .control(Control), .Cin(n1bit_alu_3_cout), .Cout(n1bit_alu_4_cout),
    .\output (Output[3]));
  _1bit_ALU u_1bit_alu_5 (
    .A(A[4]), .B(B[4]), .control(Control), .Cin(n1bit_alu_4_cout), .Cout(n1bit_alu_5_cout),
    .\output (Output[4]));
  _1bit_ALU u_1bit_alu_6 (
    .A(A[5]), .B(B[5]), .control(Control), .Cin(n1bit_alu_5_cout), .Cout(n1bit_alu_6_cout),
    .\output (Output[5]));
  _1bit_ALU u_1bit_alu_7 (
    .A(A[6]), .B(B[6]), .control(Control), .Cin(n1bit_alu_6_cout), .Cout(n1bit_alu_7_cout),
    .\output (Output[6]));
  _1bit_ALU u_1bit_alu_8 (
    .A(A[7]), .B(B[7]), .control(Control), .Cin(n1bit_alu_7_cout), .Cout(Cout), .\output (Output[7]));

  // Notes on the sheet:
  //   control bits: 0=INVA, 1=ENB, 2=ENA, 3=F1, 4=F0
endmodule

module _32bit_ALU (
  input  [31:0] A,
  input  [31:0] B,
  input  [5:0] control,
  output [31:0] Output,
  output Z,
  output N
);

  wire n8bit_alu_1_cout, n8bit_alu_2_cout, n8bit_alu_3_cout, or_1_out, or_2_out;

  _8bit_ALU u_8bit_alu_1 (
    .A(A[7:0]), .B(B[7:0]), .Control(control[5:1]), .Cin(control[0]), .Cout(n8bit_alu_1_cout),
    .Output(Output[7:0]));
  _8bit_ALU u_8bit_alu_2 (
    .A(A[15:8]), .B(B[15:8]), .Control(control[5:1]), .Cin(n8bit_alu_1_cout), .Cout(n8bit_alu_2_cout),
    .Output(Output[15:8]));
  _8bit_ALU u_8bit_alu_3 (
    .A(A[23:16]), .B(B[23:16]), .Control(control[5:1]), .Cin(n8bit_alu_2_cout), .Cout(n8bit_alu_3_cout),
    .Output(Output[23:16]));
  _8bit_ALU u_8bit_alu_4 (
    .A(A[31:24]), .B(B[31:24]), .Control(control[5:1]), .Cin(n8bit_alu_3_cout), .Output({N, Output[30:24]}));  // open: Cout
  or or_1 (or_1_out, Output[0], Output[1], Output[2], Output[3], Output[4], Output[5], Output[6], Output[7], Output[8], Output[9], Output[10], Output[11], Output[12], Output[13], Output[14], Output[15], Output[16]);
  or or_2 (or_2_out, Output[17], Output[18], Output[19], Output[20], Output[21], Output[22], Output[23], Output[24], Output[25], Output[26], Output[27], Output[28], Output[29], Output[30], N);
  nor nor_1 (Z, or_1_out, or_2_out);

  assign Output[31] = N;

  // Notes on the sheet:
  //   control bits: 0=INC, 1=INVA, 2=ENB, 3=ENA, 4=F1, 5=F0
endmodule

module datapad (
);

  wire and_1_out, and_2_out, and_4_out, d_ff_1_q, d_ff_2_q, d_ff_3_q, d_ff_4_q, d_ff_5_q, decoder_1_out0,
       decoder_1_out1, decoder_1_out2, decoder_1_out3, decoder_1_out4, decoder_1_out5, decoder_1_out6,
       decoder_1_out7, decoder_1_out8, n32bit_alu_1_n, n32bit_alu_1_z, T;
  wire [2:0] MIR2_q_2;
  wire [3:0] MIR2_q;
  wire [7:0] and_3_out, MBR_q, or_1_out, ram_2_data;
  wire [8:0] MIR2_q_3;
  wire [8:8] or_2_out;
  wire [9:0] bit_extender_1_out, bit_extender_2_out;
  wire [15:0] rom_2_data;
  wire [19:0] MIR1_q, rom_1_data;
  wire [31:0] bit_extender_3_out, bit_extender_4_out, controlled_buffer_2_out, CPP_q, H_q, LV_q, MAR_q,
       MDR_q, n32bit_alu_1_output, OPC_q, PC_q, ram_1_data, shifter_1_out, SP_q, TOS_q;

  Clock clock_1 (.out(T));
  Bit_Extender #(.in_width(32), .out_width(10)) bit_extender_1 (.in(MAR_q), .out(bit_extender_1_out));
  D_Flip_Flop d_ff_1 (.clk(T), .D(MIR2_q_2[2]), .Q(d_ff_1_q));  // open: Qn, preset, en, reset
  D_Flip_Flop d_ff_2 (.clk(T), .D(MIR2_q_2[1]), .Q(d_ff_2_q));  // open: Qn, preset, en, reset
  Bit_Extender #(.in_width(32), .out_width(10)) bit_extender_2 (.in(PC_q), .out(bit_extender_2_out));
  D_Flip_Flop d_ff_3 (.clk(T), .D(MIR2_q_2[0]), .Q(d_ff_3_q));  // open: Qn, preset, en, reset
  and and_1 (and_1_out, d_ff_1_q, T);
  RAM #(.addrWidth(10), .dataWidth(32), .bus("separate")) ram_1 (
    .addr(bit_extender_1_out), .din(MDR_q), .data(ram_1_data), .clk(and_1_out), .ld(d_ff_2_q));  // open: str, sel, clr
  RAM #(.addrWidth(10), .bus("separate")) ram_2 (
    .addr(bit_extender_2_out), .data(ram_2_data), .ld(d_ff_3_q));  // open: din, str, sel, clk, clr
  assign ram_1_data = MIR2_q_3[1] ? shifter_1_out : 32'bz;  // Controlled_Buffer controlled_buffer_1
  Register #(.width(32)) MAR (.D(shifter_1_out), .en(MIR2_q_3[0]), .Q(MAR_q), .clk(T));  // open: clr
  Register #(.width(32)) MDR (.D(ram_1_data), .Q(MDR_q), .clk(T));  // open: en, clr
  Register #(.width(32)) PC (.D(shifter_1_out), .en(MIR2_q_3[2]), .Q(PC_q), .clk(T));  // open: clr
  Register MBR (.D(ram_2_data), .Q(MBR_q), .clk(T));  // open: en, clr
  Register #(.width(32)) SP (.D(shifter_1_out), .en(MIR2_q_3[3]), .Q(SP_q), .clk(T));  // open: clr
  Register #(.width(32)) LV (.D(shifter_1_out), .en(MIR2_q_3[4]), .Q(LV_q), .clk(T));  // open: clr
  Register #(.width(32)) CPP (.D(shifter_1_out), .en(MIR2_q_3[5]), .Q(CPP_q), .clk(T));  // open: clr
  Register #(.width(32)) TOS (.D(shifter_1_out), .en(MIR2_q_3[6]), .Q(TOS_q), .clk(T));  // open: clr
  Register #(.width(32)) OPC (.D(shifter_1_out), .en(MIR2_q_3[7]), .Q(OPC_q), .clk(T));  // open: clr
  Register #(.width(32)) H (.D(shifter_1_out), .en(MIR2_q_3[8]), .Q(H_q), .clk(T));  // open: clr
  assign controlled_buffer_2_out = decoder_1_out0 ? MDR_q : 32'bz;  // Controlled_Buffer controlled_buffer_2
  assign controlled_buffer_2_out = decoder_1_out1 ? PC_q : 32'bz;  // Controlled_Buffer controlled_buffer_3
  assign bit_extender_3_out = {{24{1'b0}}, MBR_q};  // Bit_Extender bit_extender_3
  assign controlled_buffer_2_out = decoder_1_out2 ? bit_extender_3_out : 32'bz;  // Controlled_Buffer controlled_buffer_4
  assign controlled_buffer_2_out = decoder_1_out3 ? bit_extender_4_out : 32'bz;  // Controlled_Buffer controlled_buffer_5
  assign bit_extender_4_out = {{24{MBR_q[7]}}, MBR_q};  // Bit_Extender bit_extender_4
  assign controlled_buffer_2_out = decoder_1_out4 ? SP_q : 32'bz;  // Controlled_Buffer controlled_buffer_6
  assign controlled_buffer_2_out = decoder_1_out5 ? LV_q : 32'bz;  // Controlled_Buffer controlled_buffer_7
  assign controlled_buffer_2_out = decoder_1_out6 ? CPP_q : 32'bz;  // Controlled_Buffer controlled_buffer_8
  assign controlled_buffer_2_out = decoder_1_out7 ? TOS_q : 32'bz;  // Controlled_Buffer controlled_buffer_9
  assign controlled_buffer_2_out = decoder_1_out8 ? OPC_q : 32'bz;  // Controlled_Buffer controlled_buffer_10
  _32bit_ALU u_32bit_alu_1 (
    .A(H_q), .B(controlled_buffer_2_out), .control(MIR1_q[5:0]), .Output(n32bit_alu_1_output),
    .Z(n32bit_alu_1_z), .N(n32bit_alu_1_n));
  Shifter shifter_1 (.In(n32bit_alu_1_output), .SLL8(MIR1_q[7]), .SRA1(MIR1_q[6]), .Out(shifter_1_out));
  D_Flip_Flop d_ff_4 (.clk(T), .D(n32bit_alu_1_n), .Q(d_ff_4_q));  // open: Qn, preset, en, reset
  Decoder #(.select(4), .disabled(0)) decoder_1 (
    .out0(decoder_1_out0), .out1(decoder_1_out1), .out2(decoder_1_out2), .out3(decoder_1_out3),
    .out4(decoder_1_out4), .out5(decoder_1_out5), .out6(decoder_1_out6), .out7(decoder_1_out7),
    .out8(decoder_1_out8), .sel(MIR2_q));  // open: out9, out10, out11, out12, out13, out14, out15, en
  assign or_1_out = MIR1_q[18:11] | and_3_out;  // OR_Gate or_1, 8 bits wide
  or or_2 (or_2_out[8], and_2_out, and_4_out, MIR1_q[19]);
  and and_2 (and_2_out, d_ff_4_q, MIR1_q[9]);
  assign and_3_out = MBR_q & {8{MIR1_q[10]}};  // AND_Gate and_3, 8 bits wide
  and and_4 (and_4_out, d_ff_5_q, MIR1_q[8]);
  D_Flip_Flop d_ff_5 (.clk(T), .D(n32bit_alu_1_z), .Q(d_ff_5_q));  // open: Qn, preset, en, reset
  Register #(.width(20), .trigger("falling")) MIR1 (.D(rom_1_data), .Q(MIR1_q), .clk(T));  // open: en, clr
  ROM #(.addrWidth(9), .dataWidth(20)) rom_1 (.addr({or_2_out[8], or_1_out}), .data(rom_1_data));  // open: sel
  Register #(.width(16), .trigger("falling")) MIR2 (
    .D(rom_2_data), .Q({MIR2_q_3, MIR2_q_2, MIR2_q}), .clk(T));  // open: en, clr
  ROM #(.addrWidth(9), .dataWidth(16)) rom_2 (.addr({or_2_out[8], or_1_out}), .data(rom_2_data));  // open: sel

  // Notes on the sheet:
  //   C
  //   A
  //   B
  //   Control store 1
  //   contents of rom_1 (hex, n*v repeats v):
  //   835 35
  //   Control store 2
  //   contents of rom_2 (hex, n*v repeats v):
  //   211 201
endmodule

module Shifter (
  input  [31:0] In,
  input  SLL8,
  input  SRA1,
  output [31:0] Out
);

  wire shift_right_1bit_1_rightbit_out, shift_right_1bit_2_rightbit_out, shift_right_1bit_3_rightbit_out;
  wire [7:0] and_1_out, and_2_out, and_3_out, and_4_out, and_5_out, and_6_out, and_7_out, and_8_out,
       or_1_out, or_2_out, or_3_out, or_4_out;
  wire [7:7] not_1_out;

  assign and_1_out = {8{not_1_out[7]}} & In[31:24];  // AND_Gate and_1, 8 bits wide
  assign or_1_out = and_1_out | and_2_out;  // OR_Gate or_1, 8 bits wide
  assign and_2_out = {8{SLL8}} & In[23:16];  // AND_Gate and_2, 8 bits wide
  assign and_3_out = {8{not_1_out[7]}} & In[23:16];  // AND_Gate and_3, 8 bits wide
  Shift_Right_1bit shift_right_1bit_1 (
    .leftbit_in(or_1_out[7]), .SR1(SRA1), .In(or_1_out), .Out(Out[31:24]),
    .rightbit_out(shift_right_1bit_1_rightbit_out));
  assign and_4_out = {8{SLL8}} & In[15:8];  // AND_Gate and_4, 8 bits wide
  assign and_5_out = {8{not_1_out[7]}} & In[15:8];  // AND_Gate and_5, 8 bits wide
  assign or_2_out = and_3_out | and_4_out;  // OR_Gate or_2, 8 bits wide
  Shift_Right_1bit shift_right_1bit_2 (
    .leftbit_in(shift_right_1bit_1_rightbit_out), .SR1(SRA1), .In(or_2_out), .Out(Out[23:16]),
    .rightbit_out(shift_right_1bit_2_rightbit_out));
  assign and_6_out = {8{SLL8}} & In[7:0];  // AND_Gate and_6, 8 bits wide
  assign or_3_out = and_5_out | and_6_out;  // OR_Gate or_3, 8 bits wide
  Shift_Right_1bit shift_right_1bit_3 (
    .leftbit_in(shift_right_1bit_2_rightbit_out), .SR1(SRA1), .In(or_3_out), .Out(Out[15:8]),
    .rightbit_out(shift_right_1bit_3_rightbit_out));
  assign and_7_out = {8{not_1_out[7]}} & In[7:0];  // AND_Gate and_7, 8 bits wide
  assign and_8_out = {8{SLL8}} & {8{1'b0}};  // AND_Gate and_8, 8 bits wide
  assign or_4_out = and_7_out | and_8_out;  // OR_Gate or_4, 8 bits wide
  Shift_Right_1bit shift_right_1bit_4 (
    .leftbit_in(shift_right_1bit_3_rightbit_out), .SR1(SRA1), .In(or_4_out), .Out(Out[7:0]));  // open: rightbit_out
  not not_1 (not_1_out[7], SLL8);
endmodule

module Shift_Right_1bit (
  input  [7:0] In,
  input  leftbit_in,
  input  SR1,
  output rightbit_out,
  output [7:0] Out
);

  wire and_1_out, and_2_out, and_3_out, and_4_out, and_5_out, and_6_out, and_7_out, and_8_out, and_9_out,
       and_10_out, and_11_out, and_12_out, and_13_out, and_14_out, and_15_out, and_16_out, not_1_out;

  not not_1 (not_1_out, SR1);
  and and_1 (and_1_out, SR1, leftbit_in);
  and and_2 (and_2_out, not_1_out, In[7]);
  or or_1 (Out[7], and_1_out, and_2_out);
  and and_3 (and_3_out, SR1, In[7]);
  or or_2 (Out[6], and_3_out, and_5_out);
  and and_4 (and_4_out, SR1, In[6]);
  and and_5 (and_5_out, not_1_out, In[6]);
  or or_3 (Out[5], and_4_out, and_7_out);
  and and_6 (and_6_out, SR1, In[5]);
  and and_7 (and_7_out, not_1_out, In[5]);
  and and_8 (and_8_out, not_1_out, In[4]);
  and and_9 (and_9_out, SR1, In[4]);
  or or_4 (Out[4], and_6_out, and_8_out);
  and and_10 (and_10_out, not_1_out, In[3]);
  or or_5 (Out[3], and_9_out, and_10_out);
  and and_11 (and_11_out, not_1_out, In[2]);
  and and_12 (and_12_out, SR1, In[3]);
  or or_6 (Out[2], and_12_out, and_11_out);
  and and_13 (and_13_out, SR1, In[2]);
  and and_14 (and_14_out, not_1_out, In[1]);
  or or_7 (Out[1], and_13_out, and_14_out);
  and and_15 (and_15_out, SR1, In[1]);
  and and_16 (and_16_out, not_1_out, In[0]);
  or or_8 (Out[0], and_15_out, and_16_out);

  assign rightbit_out = In[0];
endmodule
