// Logisim project microcomputer.circ as structural Verilog: 4 circuits, main circuit datapad
module datapad (
  input  CS1,
  input  CS9,
  input  CS2,
  input  CS10,
  input  CS3,
  input  CS11,
  input  CS4,
  input  CS12,
  input  CS_MPC,
  input  CS22,
  input  CS5,
  input  CS17,
  input  CS_MIR,
  input  CS18,
  input  CS19,
  input  CS20,
  input  CS21,
  input  CS6,
  input  CS13,
  input  CS15,
  input  CS16,
  input  CS7,
  input  CS8,
  input  CS14,
  output [21:0] MIR_control_signals
);

  wire or_1_out;
  wire [5:0] MPC_q_2;
  wire [9:0] MPC_q;
  wire [9:9] not_1_out;
  wire [15:0] A_q, alu_1_out_5, B_q, C_q, controlled_buffer_1_out, controlled_buffer_4_out,
       controlled_buffer_9_out, D_q, MAR_q, MDR_q, ram_1_data, test_a_1_msb, test_a_1_zero;
  wire [15:4] undriven;
  wire [21:0] rom_1_data;
  wire [21:12] MIR_q;

  Register #(.width(16), .trigger("high")) MAR (.D(alu_1_out_5), .Q(MAR_q), .clk(CS14));  // open: en, clr
  assign controlled_buffer_1_out = CS13 ? alu_1_out_5 : 16'bz;  // Controlled_Buffer controlled_buffer_1
  or or_1 (or_1_out, CS16, CS15);
  Register #(.width(16), .trigger("high")) A (.D(alu_1_out_5), .Q(A_q), .clk(CS9));  // open: en, clr
  Register #(.width(16), .trigger("high")) B (.D(alu_1_out_5), .Q(B_q), .clk(CS10));  // open: en, clr
  Register #(.width(16), .trigger("high")) C (.D(alu_1_out_5), .Q(C_q), .clk(CS11));  // open: en, clr
  Register #(.width(16), .trigger("high")) D (.D(alu_1_out_5), .Q(D_q), .clk(CS12));  // open: en, clr
  Register #(.width(16), .trigger("high")) MPC (.D(alu_1_out_5), .Q({MPC_q_2, MPC_q}), .clk(CS_MPC));  // open: en, clr
  ROM #(.addrWidth(10), .dataWidth(22)) rom_1 (.addr(MPC_q), .data(rom_1_data));  // open: sel
  Test_A test_a_1 (.A_in(A_q), .zero(test_a_1_zero), .msb(test_a_1_msb));
  assign controlled_buffer_1_out = CS15 ? ram_1_data : 16'bz;  // Controlled_Buffer controlled_buffer_2
  RAM #(.addrWidth(12), .dataWidth(16), .bus("asynch")) ram_1 (
    .addr(MAR_q[11:0]), .data(ram_1_data), .sel(or_1_out), .ld(CS15));  // open: clr
  Register #(.width(22), .trigger("high")) MIR (
    .D(rom_1_data), .Q({MIR_q, MIR_control_signals[11:0]}), .clk(CS_MIR));  // open: en, clr
  assign MIR_control_signals[21:12] = MIR_q & {10{not_1_out[9]}};  // AND_Gate and_1, 10 bits wide
  Register #(.width(16), .trigger("high")) MDR (.D(controlled_buffer_1_out), .Q(MDR_q), .clk(1'b1));  // open: en, clr
  assign ram_1_data = CS16 ? MDR_q : 16'bz;  // Controlled_Buffer controlled_buffer_3
  assign controlled_buffer_4_out = CS1 ? A_q : 16'bz;  // Controlled_Buffer controlled_buffer_4
  assign controlled_buffer_4_out = CS2 ? B_q : 16'bz;  // Controlled_Buffer controlled_buffer_5
  assign controlled_buffer_4_out = CS3 ? C_q : 16'bz;  // Controlled_Buffer controlled_buffer_6
  assign controlled_buffer_4_out = CS4 ? D_q : 16'bz;  // Controlled_Buffer controlled_buffer_7
  assign controlled_buffer_4_out = CS22 ? {MPC_q_2, MPC_q} : 16'bz;  // Controlled_Buffer controlled_buffer_8
  assign controlled_buffer_9_out = CS5 ? 16'h1 : 16'bz;  // Controlled_Buffer controlled_buffer_9
  assign controlled_buffer_9_out = CS17 ? 16'h1 : 16'bz;  // Controlled_Buffer controlled_buffer_10
  assign controlled_buffer_9_out = CS18 ? {{6{1'b0}}, MIR_q} : 16'bz;  // Controlled_Buffer controlled_buffer_11
  not not_1 (not_1_out[9], CS18);
  assign controlled_buffer_9_out = CS19 ? test_a_1_zero : 16'bz;  // Controlled_Buffer controlled_buffer_12
  assign controlled_buffer_9_out = CS20 ? test_a_1_msb : 16'bz;  // Controlled_Buffer controlled_buffer_13
  assign controlled_buffer_9_out = CS21 ? {undriven, MDR_q[15:12]} : 16'bz;  // Controlled_Buffer controlled_buffer_14
  assign controlled_buffer_9_out = CS6 ? MDR_q : 16'bz;  // Controlled_Buffer controlled_buffer_15
  ALU alu_1 (
    .in_1(controlled_buffer_4_out), .in_2(controlled_buffer_9_out), .Substract(CS7), .Shift_left(CS8),
    .out_5(alu_1_out_5));

  // Notes on the sheet:
  //   Micro Memory
  //   Main Memory
  //   contents of rom_1 (hex, n*v repeats v):
  //   221 9 5010 90221 22a020 20161
  //   BUS 1
  //   BUS 2
  //   ALU
  //   BUS 3
endmodule

module ALU (
  input  [15:0] in_1,
  input  [15:0] in_2,
  input  Substract,
  input  Shift_left,
  output [15:0] out_5
);

  wire [15:0] adder_1_out, xor_1_out;

  assign xor_1_out = in_2 ^ {16{Substract}};  // XOR_Gate xor_1, 16 bits wide
  Adder #(.width(16)) adder_1 (.a(in_1), .b(xor_1_out), .out(adder_1_out), .cin(Substract));  // open: cout
  Shifter #(.width(16), .shift("ll")) shifter_1 (.in(adder_1_out), .\dist ({3'b000, Shift_left}), .out(out_5));

  // Notes on the sheet:
  //   in_1: pull=down
  //   in_2: pull=down
endmodule

module Test_A (
  input  [15:0] A_in,
  output [15:0] zero,
  output [15:0] msb
);

  wire nor_1_out, not_1_out, not_2_out, or_1_out, or_2_out;

  or or_1 (or_1_out, A_in[0], A_in[1], A_in[2], A_in[3], A_in[4], A_in[5], A_in[6]);
  or or_2 (or_2_out, A_in[7], A_in[8], A_in[9], A_in[10], A_in[11], A_in[12], A_in[13], A_in[14], A_in[15]);
  nor nor_1 (nor_1_out, or_1_out, or_2_out);
  not not_1 (not_1_out, nor_1_out);
  not not_2 (not_2_out, A_in[15]);
  assign zero = nor_1_out ? 16'h1 : 16'bz;  // Controlled_Buffer controlled_buffer_1
  assign zero = not_1_out ? 16'h2 : 16'bz;  // Controlled_Buffer controlled_buffer_2
  assign msb = A_in[15] ? 16'h1 : 16'bz;  // Controlled_Buffer controlled_buffer_3
  assign msb = not_2_out ? 16'h2 : 16'bz;  // Controlled_Buffer controlled_buffer_4
endmodule

module main (
);

  wire clock_1_out, decoder_1_out4;
  wire [1:0] and_2_out;
  wire [1:1] decoder_1_out2;
  wire [2:0] counter_1_q;
  wire [5:0] and_1_out, and_3_out;
  wire [5:5] decoder_1_out1, decoder_1_out3;
  wire [7:0] and_4_out;
  wire [7:7] decoder_1_out0;
  wire [21:0] datapad_1_mir_control_signals;

  Clock #(.highDuration(1), .lowDuration(1)) clock_1 (.out(clock_1_out));
  Counter #(.width(3), .max(4), .trigger("rising")) counter_1 (
    .Q(counter_1_q), .clk(clock_1_out));  // open: load, D, count, carry, clr
  Decoder #(.select(3), .tristate("false")) decoder_1 (
    .out0(decoder_1_out0[7]), .out1(decoder_1_out1[5]), .out2(decoder_1_out2[1]), .out3(decoder_1_out3[5]),
    .out4(decoder_1_out4), .sel(counter_1_q));  // open: out5, out6, out7
  assign and_1_out = datapad_1_mir_control_signals[13:8] & {6{decoder_1_out1[5]}};  // AND_Gate and_1, 6 bits wide
  assign and_2_out = datapad_1_mir_control_signals[7:6] & {2{decoder_1_out2[1]}};  // AND_Gate and_2, 2 bits wide
  assign and_3_out = datapad_1_mir_control_signals[5:0] & {6{decoder_1_out3[5]}};  // AND_Gate and_3, 6 bits wide
  assign and_4_out = datapad_1_mir_control_signals[21:14] & {8{decoder_1_out0[7]}};  // AND_Gate and_4, 8 bits wide
  datapad datapad_1 (
    .CS9(and_1_out[5]), .CS10(and_1_out[4]), .CS11(and_1_out[3]), .CS12(and_1_out[2]), .CS13(and_1_out[1]),
    .CS14(and_1_out[0]), .MIR_control_signals(datapad_1_mir_control_signals), .CS15(and_2_out[1]),
    .CS16(and_2_out[0]), .CS_MPC(decoder_1_out4), .CS_MIR(decoder_1_out4), .CS1(and_4_out[7]),
    .CS2(and_4_out[6]), .CS3(and_4_out[5]), .CS4(and_4_out[4]), .CS5(and_4_out[3]), .CS6(and_4_out[2]),
    .CS7(and_4_out[1]), .CS8(and_4_out[0]), .CS22(and_3_out[0]), .CS17(and_3_out[5]), .CS18(and_3_out[4]),
    .CS19(and_3_out[3]), .CS20(and_3_out[2]), .CS21(and_3_out[1]));
endmodule
